// Logisim project li_zhijian.circ as structural Verilog
module main (
);

  wire CLK, comparator_1_eq;
  wire [3:0] if_idrr_buffer_1_op_out, if_idrr_buffer_1_rx_out, if_idrr_buffer_1_ry_out,
       if_idrr_buffer_1_rz_out;
  wire [19:0] if_idrr_buffer_1_imm_out;
  wire [31:0] adder_1_out, adder_2_out, bit_extender_1_out, i_mem_1_ir_out, if_idrr_buffer_1_pc_out,
       multiplexer_1_out, PC_q, regs_1_a, regs_1_b;

  Clock CLOCK (.out(CLK));
  Adder #(.width(32)) adder_1 (.a(PC_q), .b(32'h1), .out(adder_1_out));  // open: cin, cout
  I_MEM i_mem_1 (.PC_IN(PC_q), .IR_OUT(i_mem_1_ir_out), .in_1(CLK));
  Multiplexer #(.select(2), .width(32), .enable("false")) multiplexer_1 (
    .in0(adder_1_out), .out(multiplexer_1_out));  // open: in1, in2, in3, sel
  Register #(.width(32)) PC (.D(multiplexer_1_out), .Q(PC_q), .clk(CLK));  // open: en, clr
  IF_IDRR_Buffer if_idrr_buffer_1 (
    .in_1(CLK), .PC_N(adder_1_out), .IR_IN(i_mem_1_ir_out), .PC_OUT(if_idrr_buffer_1_pc_out),
    .OP_OUT(if_idrr_buffer_1_op_out), .RX_OUT(if_idrr_buffer_1_rx_out), .RY_OUT(if_idrr_buffer_1_ry_out),
    .RZ_OUT(if_idrr_buffer_1_rz_out), .IMM_OUT(if_idrr_buffer_1_imm_out));
  assign bit_extender_1_out = {{12{if_idrr_buffer_1_imm_out[19]}}, if_idrr_buffer_1_imm_out};  // Bit_Extender bit_extender_1
  Regs regs_1 (
    .OP_IN(if_idrr_buffer_1_op_out), .RX_IN(if_idrr_buffer_1_rx_out), .RY_IN(if_idrr_buffer_1_ry_out),
    .RZ_IN(if_idrr_buffer_1_rz_out), .CK(CLK), .A(regs_1_a), .B(regs_1_b));  // open: Use_IMM, ALU, BEQ, JALR, LEA, STR
  Adder #(.width(32)) adder_2 (
    .a(bit_extender_1_out), .b(if_idrr_buffer_1_pc_out), .out(adder_2_out));  // open: cin, cout
  Comparator #(.width(32)) comparator_1 (.a(regs_1_b), .b(regs_1_a), .eq(comparator_1_eq));  // open: gt, lt
endmodule

module Dual_Ported_Register_File (
  input  CLK,
  input  WrEN,
  input  [3:0] WrREGNO,
  input  [3:0] RdREGNO1,
  input  [3:0] RdREGNO2,
  input  [31:0] INPUT,
  output [31:0] OUT1,
  output [31:0] OUT2
);

  wire En_a0, En_a1, En_a2, En_at, En_fp, En_k0, En_ra, En_s0, En_s1, En_s2, En_sp, En_t0, En_t1, En_t2,
       En_v0;
  wire [31:0] a0, a1, a2, at, fp, k0, ra, s0, s1, s2, sp, t0, t1, t2, v0, zero;

  Decoder #(.select(4), .disabled(0)) decoder_1 (
    .out1(En_at), .out2(En_v0), .out3(En_a0), .out4(En_a1), .out5(En_a2), .out6(En_t0), .out7(En_t1),
    .out8(En_t2), .out9(En_s0), .out10(En_s1), .out11(En_s2), .out12(En_k0), .out13(En_sp), .out14(En_fp),
    .out15(En_ra), .sel(WrREGNO), .en(WrEN));  // open: out0
  Register #(.width(32)) u_zero (.D(INPUT), .en(1'b0), .Q(zero), .clk(CLK));  // open: clr
  Register #(.width(32)) u_at (.D(INPUT), .en(En_at), .Q(at), .clk(CLK));  // open: clr
  Register #(.width(32)) u_v0 (.D(INPUT), .en(En_v0), .Q(v0), .clk(CLK));  // open: clr
  Register #(.width(32)) u_a0 (.D(INPUT), .en(En_a0), .Q(a0), .clk(CLK));  // open: clr
  Register #(.width(32)) u_a1 (.D(INPUT), .en(En_a1), .Q(a1), .clk(CLK));  // open: clr
  Register #(.width(32)) u_a2 (.D(INPUT), .en(En_a2), .Q(a2), .clk(CLK));  // open: clr
  Register #(.width(32)) u_t0 (.D(INPUT), .en(En_t0), .Q(t0), .clk(CLK));  // open: clr
  Register #(.width(32)) u_t1 (.D(INPUT), .en(En_t1), .Q(t1), .clk(CLK));  // open: clr
  Multiplexer #(.select(4), .width(32), .disabled(0), .enable("false")) multiplexer_1 (
    .in0(zero), .in1(at), .in2(v0), .in3(a0), .in4(a1), .in5(a2), .in6(t0), .in7(t1), .in8(t2), .in9(s0),
    .in10(s1), .in11(s2), .in12(k0), .in13(sp), .in14(fp), .in15(ra), .out(OUT2), .sel(RdREGNO2));
  Register #(.width(32)) u_t2 (.D(INPUT), .en(En_t2), .Q(t2), .clk(CLK));  // open: clr
  Register #(.width(32)) u_s0 (.D(INPUT), .en(En_s0), .Q(s0), .clk(CLK));  // open: clr
  Register #(.width(32)) u_s1 (.D(INPUT), .en(En_s1), .Q(s1), .clk(CLK));  // open: clr
  Register #(.width(32)) u_s2 (.D(INPUT), .en(En_s2), .Q(s2), .clk(CLK));  // open: clr
  Register #(.width(32)) u_k0 (.D(INPUT), .en(En_k0), .Q(k0), .clk(CLK));  // open: clr
  Register #(.width(32)) u_sp (.D(INPUT), .en(En_sp), .Q(sp), .clk(CLK));  // open: clr
  Register #(.width(32)) u_fp (.D(INPUT), .en(En_fp), .Q(fp), .clk(CLK));  // open: clr
  Register #(.width(32)) u_ra (.D(INPUT), .en(En_ra), .Q(ra), .clk(CLK));  // open: clr
  Multiplexer #(.select(4), .width(32), .disabled(0), .enable("false")) multiplexer_2 (
    .in0(zero), .in1(at), .in2(v0), .in3(a0), .in4(a1), .in5(a2), .in6(t0), .in7(t1), .in8(t2), .in9(s0),
    .in10(s1), .in11(s2), .in12(k0), .in13(sp), .in14(fp), .in15(ra), .out(OUT1), .sel(RdREGNO1));

  // Notes on the sheet:
  //   MODIFY AT YOUR OWN RISK
endmodule

module IF_IDRR_Buffer (
  input  in_1,
  input  [31:0] PC_N,
  input  [31:0] IR_IN,
  output [31:0] PC_OUT,
  output [3:0] OP_OUT,
  output [3:0] RX_OUT,
  output [3:0] RY_OUT,
  output [3:0] RZ_OUT,
  output [19:0] IMM_OUT
);

  Register #(.width(32)) PC (.D(PC_N), .Q(PC_OUT), .clk(in_1));  // open: en, clr
  Register #(.width(32)) IR (.D(IR_IN), .Q({OP_OUT, RX_OUT, RY_OUT, IMM_OUT}), .clk(in_1));  // open: en, clr

  assign RZ_OUT = IMM_OUT[3:0];

  // Other names for the same wires on the sheet: CLK = in_1
endmodule

module I_MEM (
  input  in_1,
  input  [31:0] PC_IN,
  output [31:0] IR_OUT
);

  RAM #(.addrWidth(24), .dataWidth(32)) ram_1 (
    .addr(PC_IN[23:0]), .data(IR_OUT), .clk(in_1), .ld(1'b1));  // open: sel, clr

  // Other names for the same wires on the sheet: CLK = in_1
endmodule

module Regs (
  input  CK,
  input  [3:0] OP_IN,
  input  [3:0] RX_IN,
  input  [3:0] RY_IN,
  input  [3:0] RZ_IN,
  output [31:0] A,
  output [31:0] B,
  output Use_IMM,
  output [1:0] ALU,
  output BEQ,
  output JALR,
  output LEA,
  output STR
);

  wire Use_RZ;
  wire [3:0] multiplexer_1_out;

  Multiplexer #(.width(4), .enable("false")) multiplexer_1 (
    .in0(RX_IN), .in1(RZ_IN), .out(multiplexer_1_out), .sel(Use_RZ));
  ROM #(.addrWidth(4)) rom_1 (.addr(OP_IN), .data({Use_RZ, Use_IMM, ALU, BEQ, JALR, LEA, STR}));  // open: sel
  Dual_Ported_Register_File dual_ported_register_file_1 (
    .CLK(CK), .WrREGNO(RX_IN), .RdREGNO1(RY_IN), .RdREGNO2(multiplexer_1_out), .OUT1(A), .OUT2(B));  // open: INPUT, WrEN

  // Other names for the same wires on the sheet: CLK = CK; OP[3:0] = OP_IN; RX[3:0] = RX_IN; RY[3:0] = RY_IN;
  //   RZ[3:0] = RZ_IN
endmodule
